// Logisim project 1.circ as structural Verilog: 1 circuit, main circuit main
module main (
  input  A,
  input  in_2,
  input  B,
  input  Cout,
  input  Cin,
  output out_6
);

  wire adder_1_cout, adder_1_out, and_1_out, not_1_out, or_1_out, undriven;
  wire [1:0] undriven_2;

  and and_1 (and_1_out, A, A);
  not not_1 (not_1_out, A);
  or or_1 (or_1_out, A, A);
  Adder #(.width(1)) adder_1 (.b(A), .out(adder_1_out), .cin(undriven), .cout(adder_1_cout));  // open: a
  Multiplexer #(.select(2), .enable("false")) multiplexer_1 (
    .in0(and_1_out), .in1(not_1_out), .in2(or_1_out), .in3(undriven), .out(out_6), .sel(undriven_2));

  assign B = A;

  // Notes on the sheet:
  //   A and B
  //   0  0
  //   NOT b
  //   0 1
  //   a OR b
  //   1 0
  //   a-b
  //   a+b
  //   1 1
endmodule
