// Logisim project 1b.circ as structural Verilog: 1 circuit, main circuit main
module main (
  input  A,
  input  B,
  input  C,
  input  G,
  input  R,
  input  B_2
);

  wire decoder_1_out0, decoder_1_out1, decoder_1_out2, decoder_1_out3, decoder_1_out4, decoder_1_out5,
       decoder_1_out6, decoder_1_out7, OR_2_out, OR_out, undriven;
  wire [2:0] undriven_2;

  Decoder #(.select(3), .tristate("true")) decoder_1 (
    .out0(decoder_1_out0), .out1(decoder_1_out1), .out2(decoder_1_out2), .out3(decoder_1_out3),
    .out4(decoder_1_out4), .out5(decoder_1_out5), .out6(decoder_1_out6), .out7(decoder_1_out7),
    .sel(undriven_2), .en(undriven));
  or OR (OR_out, decoder_1_out7, decoder_1_out6, decoder_1_out4, decoder_1_out2);
  or OR_2 (OR_2_out, decoder_1_out7, decoder_1_out6, decoder_1_out3);

  // Notes on the sheet:
  //   ABC
  //   000
  //   001
  //   010
  //   011
  //   3-8
  //   100
  //   101
  //   110
  //   111
endmodule
