// Logisim project 8NUMBER.circ as structural Verilog: 1 circuit, main circuit main
module main (
  input  X,
  input  Y,
  input  Z,
  output R,
  output G,
  output B
);

  wire and_1_out, and_2_out, and_3_out, and_4_out, not_1_out, not_2_out;

  not not_1 (not_1_out, Y);
  and and_1 (and_1_out, X, Z);
  not not_2 (not_2_out, Z);
  and and_2 (and_2_out, X, not_1_out);
  or or_1 (G, Y, and_1_out);
  and and_3 (and_3_out, X, not_2_out);
  and and_4 (and_4_out, X, Y);
  or or_2 (R, Z, and_2_out);
  or or_3 (B, and_3_out, and_4_out);
endmodule
