// Logisim project number 8 .circ as structural Verilog: 1 circuit, main circuit main
module main (
  input  R,
  input  G,
  input  B,
  output P
);

  wire and_1_out, and_2_out, and_3_out, not_1_out, not_2_out;

  not not_1 (not_1_out, R);
  not not_2 (not_2_out, G);
  and and_1 (and_1_out, not_1_out, G);
  and and_2 (and_2_out, R, not_2_out);
  and and_3 (and_3_out, R, B);
  or or_1 (P, and_1_out, and_2_out, and_3_out);

  // Notes on the sheet:
  //   8.
endmodule
