// Logisim project number 9.circ as structural Verilog: 1 circuit, main circuit main
module main (
  input  M,
  input  S,
  input  E,
  input  H,
  output G
);

  wire and_1_out;

  and and_1 (and_1_out, M, S);
  or or_1 (G, H, E, and_1_out);

  // Notes on the sheet:
  //   9. 
endmodule
